# Fritzing sketch CalmPalm_fritz (saved by Fritzing 1.0.1rc)
breadboards: 1

parts:
  A1 = Particle - Photon2
  SW1 = DIP SWITCH [package=dipswitch-02]
  SW2 = DIP SWITCH [package=dipswitch-02]
  Grove1 = Grove OLED 128x96
  Neopixel1 = Adafruit RBG Smart Neopixel [package="DIP (Dual Inline) [THT]"]
  U1 = ENCODER-QUADRATURE [package=encoder-16mm-quad]
  R1 = Resistor [tolerance=±5% power=0.25W resistance=220 package=THT]

nets (from the breadboard view):
  N1: A1.Pin_4, A1.Pin_32
  N2: A1.Pin_7, SW1.2
  N3: A1.Pin_8, SW1.1
  N4: A1.Pin_9, SW2.2
  N5: A1.Pin_10, SW2.1
  N6: A1.Pin_13, U1.C, R1.Pin_0
  N7: A1.Pin_14, U1.B
  N8: A1.Pin_15, U1.A
  N9: A1.Pin_17, Grove1.SDA
  N10: A1.Pin_18, Grove1.SCL
  N11: A1.Pin_19, Neopixel1.In
  N12: SW1.3, SW2.3, Grove1.VCC, Neopixel1.+, R1.Pin_1
  N13: Grove1.GND, Neopixel1.G

notes:
  4 dip switch combo
  Adafruit 5x5 Neopixel Grid

custom parts:
  Particle - Photon2: The Photon 2 is a microcontroller and Wi-Fi networking developed by particle. Features: 802.11a/b/g/n Wi-Fi, 2.4 GHz and 5 GHz Integrated PCB antenna Integrated U.FL connector for external antenna Integrated RF switch BLE 5 using same antenna as Wi-Fi Realtek RTL8721DM MCU ARM Cortex M33 CPU, 200 MHz 2048 KB (2 MB) user application maximum size 3072 KB (3 MB) of RAM available to user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
